# Fritzing sketch AllSensors (saved by Fritzing 0.9.2b)
breadboards: 1

parts:
  Part1 = Arduino Yun
  R1 = Resistor [tolerance=±5% resistance=10k package=THT]
  R2 = Textile Stretch Sensor [part_number=PW052]
  Pulse_Sensor1 = TSOP312.., 314.. [part_number=Pulse package=THT]

nets:
  N1: Part1.A0, R1.Pin_1, R2.pin_0
  N2: Part1.A1, Pulse_Sensor1.Data
  N3: Part1.AREF, Part1.3V3, R1.Pin_0, Pulse_Sensor1.Vs
  GND: Part1.GND, R2.pin_1, Pulse_Sensor1.GND
