# Fritzing sketch PulseSensor (saved by Fritzing 0.9.2b)
breadboards: 1

parts:
  Pulse_Sensor = TSOP312.., 314.. [part_number=Pulse package=THT]
  Part1 = Arduino Yun

nets:
  GND: Pulse_Sensor.GND, Part1.GND
  N1: Pulse_Sensor.Vs, Part1.AREF, Part1.3V3
  N2: Pulse_Sensor.Data, Part1.A0
