# Fritzing sketch StretchSensor (saved by Fritzing 0.9.2b)
breadboards: 1

parts:
  Part1 = Arduino Yun
  R1 = Resistor [tolerance=±5% resistance=10k package=THT]
  R2 = Textile Stretch Sensor [part_number=PW052]

nets:
  N1: Part1.A0, R1.Pin_1, R2.pin_0
  N2: Part1.AREF, Part1.3V3, R1.Pin_0
  N3: Part1.GND, R2.pin_1
