# Fritzing sketch eda (saved by Fritzing 0.9.4)
breadboards: 1

parts:
  Composants1 = Arduino Due (Rev2b)
  IC3 = DIP - 8 pins [chip_label=ICL7660 package="DIP (Dual Inline) [THT]"]
  D1 = Rectifier Diode [part_number=1N4007 package="300 mil [THT]"]
  D2 = Rectifier Diode [part_number=1N4007 package="300 mil [THT]"]
  C1 = Electrolytic Capacitor [capacitance=10μF voltage=25V package="0605 [SMD, electrolytic]"]
  C2 = Electrolytic Capacitor [capacitance=10μF voltage=25V package="0605 [SMD, electrolytic]"]  # not connected
  IC4 = Dual Op-Amp [part_number=TLC2272ACPE4 package=dip08]
  R1 = Resistor [tolerance=±5% resistance=1M package=THT]
  R2 = Resistor [tolerance=±5% resistance=100k package=THT]
  R3 = Resistor [tolerance=±5% resistance=100k package=THT]
  R4 = Resistor [tolerance=±5% resistance=100k package=THT]
  C4 = Ceramic Capacitor [capacitance=100nF package="100 mil [THT, multilayer]"]
  C2_2 = Ceramic Capacitor [capacitance=100nF package="100 mil [THT, multilayer]"]
  C3 = Ceramic Capacitor [capacitance=100nF package="100 mil [THT, multilayer]"]
  C1_2 = Ceramic Capacitor [capacitance=100nF package="100 mil [THT, multilayer]"]
  R5 = Resistor [tolerance=±5% resistance=100k package=THT]

nets:
  N1: Composants1.A0, IC4.B_OUT, R1.Pin_1, R3.Pin_0, C1_2.1
  N2: Composants1.A1, IC4.A_OUT, IC4.B_+IN, R2.Pin_0, C3.0
  N3: Composants1.IOREF, IC3.V+, D1.anode, R4.Pin_0, C2_2.1
  GND: Composants1.GND, IC3.GND, IC3.Vout, IC3.LV, IC4.A_V-, C4.1, C2_2.0, R5.Pin_1
  N4: IC3.CAP+, C1.-
  N5: D1.cathode, D2.anode, C1.+
  N6: D2.cathode, IC4.A_V+
  N7: IC4.A_-IN, R2.Pin_1, R3.Pin_1, C3.1
  N8: IC4.A_+IN, R4.Pin_1, C4.0, R5.Pin_0
  N9: IC4.B_-IN, R1.Pin_0, C1_2.0

notes:
  step-up voltage from 3.3v to approx. 5.2V (double voltage minus drop from diodes)
  3.3v rail
  5v+ rail
  om-amp: TLC2272ACPE4
  pump: ICL7660EPA+
  NB: used "regular" ceramic capacitor for real
  to the skin
  Vb
  bias
  Vo
  out
  diode: 1N4007
  ceramic capacitor: 100nf
  electrolytic capacitor: 10uf

custom parts:
  DIP - 8 pins: Switched-cappacitor voltage converter
